// Logisim project 4_bit D Flip Flop.circ as structural Verilog: 1 circuit, main circuit main
module main (
  input  D_1,
  input  D_3,
  input  Clock,
  input  D_2,
  input  D_4,
  output out_6,
  output out_7,
  output out_8,
  output out_9,
  output out_10,
  output out_11,
  output out_12,
  output out_13
);

  wire nand_1_out, nand_2_out, nand_5_out, nand_6_out, nand_9_out, nand_10_out, nand_13_out, nand_14_out,
       not_1_out, not_2_out, not_3_out, not_4_out;

  not not_1 (not_1_out, D_1);
  not not_2 (not_2_out, D_2);
  nand nand_1 (nand_1_out, D_1, Clock);
  nand nand_2 (nand_2_out, Clock, not_1_out);
  nand nand_3 (out_6, nand_1_out, out_8);
  nand nand_4 (out_8, out_6, nand_2_out);
  nand nand_5 (nand_5_out, D_2, Clock);
  nand nand_6 (nand_6_out, Clock, not_2_out);
  nand nand_7 (out_10, nand_5_out, out_12);
  nand nand_8 (out_12, out_10, nand_6_out);
  not not_3 (not_3_out, D_3);
  nand nand_9 (nand_9_out, D_3, Clock);
  nand nand_10 (nand_10_out, Clock, not_3_out);
  not not_4 (not_4_out, D_4);
  nand nand_11 (out_7, nand_9_out, out_9);
  nand nand_12 (out_9, out_7, nand_10_out);
  nand nand_13 (nand_13_out, D_4, Clock);
  nand nand_14 (nand_14_out, Clock, not_4_out);
  nand nand_15 (out_11, nand_13_out, out_13);
  nand nand_16 (out_13, out_11, nand_14_out);
endmodule
